// Logisim project stage1.circ as structural Verilog: 2 circuits, main circuit main
module main (
);

  wire button_1_out, button_3_out, subcircuit_stage1_1_o;

  subcircuit_stage1 subcircuit_stage1_1 (.i(button_1_out), .resetIN(button_3_out), .o(subcircuit_stage1_1_o));
  Hex_Digit_Display hex_digit_display_1 ();  // open: value, dp
  Button button_1 (.out(button_1_out));
  Hex_Digit_Display hex_digit_display_2 ();  // open: value, dp
  Hex_Digit_Display hex_digit_display_3 ();  // open: value, dp
  Hex_Digit_Display hex_digit_display_4 ();  // open: value, dp
  Button button_2 ();  // open: out
  Button button_3 (.out(button_3_out));
  Hex_Digit_Display hex_digit_display_5 ();  // open: value, dp
  Hex_Digit_Display hex_digit_display_6 ();  // open: value, dp
  Hex_Digit_Display hex_digit_display_7 ();  // open: value, dp
  Hex_Digit_Display hex_digit_display_8 ();  // open: value, dp
  LED led_1 (.in(subcircuit_stage1_1_o));

  // Notes on the sheet:
  //   Minutes
  //   Start/Stop
  //   Elapsed Time
  //   Seconds
  //   Stopwatch Interface
  //   Split
  //   Reset
  //   Minutes
  //   Split time
  //   Seconds
  //   Clock Started
endmodule

module subcircuit_stage1 (
  input  i,
  input  resetIN,
  output o
);

  T_Flip_Flop t_ff_1 (.T(1'b1), .clk(i), .Q(o), .reset(resetIN));  // open: Qn, preset
endmodule
