// Logisim project stage4.circ as structural Verilog: 5 circuits, main circuit main
module main (
);

  wire button_1_out, button_3_out, subcircuit_stage1_1_onoff, subcircuit_stage2_1_bufferclock,
       subcircuit_stage2_1_co, subcircuit_stage3_1_co;
  wire [3:0] subcircuit_stage2_1_o, subcircuit_stage3_1_o, subcircuit_stage4_1_ones, subcircuit_stage4_1_tens;

  subcircuit_stage1 subcircuit_stage1_1 (.i(button_1_out), .Resetin(button_3_out), .onOFF(subcircuit_stage1_1_onoff));
  subcircuit_stage2 subcircuit_stage2_1 (
    .i(button_1_out), .Resetin(button_3_out), .Co(subcircuit_stage2_1_co), .O(subcircuit_stage2_1_o),
    .bufferCLOCK(subcircuit_stage2_1_bufferclock));
  subcircuit_stage3 subcircuit_stage3_1 (
    .Ci(subcircuit_stage2_1_co), .bufferCLOCK(subcircuit_stage2_1_bufferclock), .Resetin(button_3_out),
    .Co(subcircuit_stage3_1_co), .O(subcircuit_stage3_1_o));
  Hex_Digit_Display hex_digit_display_1 (.value(subcircuit_stage4_1_tens));  // open: dp
  subcircuit_stage4 subcircuit_stage4_1 (
    .Ci(subcircuit_stage3_1_co), .bufferCLOCK(subcircuit_stage2_1_bufferclock), .Resetin(button_3_out),
    .ones(subcircuit_stage4_1_ones), .tens(subcircuit_stage4_1_tens));
  Button button_1 (.out(button_1_out));
  Hex_Digit_Display hex_digit_display_2 (.value(subcircuit_stage4_1_ones));  // open: dp
  Hex_Digit_Display hex_digit_display_3 (.value(subcircuit_stage3_1_o));  // open: dp
  Hex_Digit_Display hex_digit_display_4 (.value(subcircuit_stage2_1_o));  // open: dp
  Button button_2 ();  // open: out
  Button button_3 (.out(button_3_out));
  Hex_Digit_Display hex_digit_display_5 ();  // open: value, dp
  Hex_Digit_Display hex_digit_display_6 ();  // open: value, dp
  Hex_Digit_Display hex_digit_display_7 ();  // open: value, dp
  Hex_Digit_Display hex_digit_display_8 ();  // open: value, dp
  LED led_1 (.in(subcircuit_stage1_1_onoff));

  // Notes on the sheet:
  //   Minutes
  //   Start/Stop
  //   Elapsed Time
  //   Seconds
  //   Stopwatch Interface
  //   Split
  //   Reset
  //   Minutes
  //   Split time
  //   Seconds
  //   Clock Started
endmodule

module subcircuit_stage1 (
  input  i,
  input  Resetin,
  output onOFF
);

  T_Flip_Flop t_ff_1 (.T(1'b1), .clk(i), .Q(onOFF), .reset(Resetin));  // open: Qn, preset
endmodule

module subcircuit_stage2 (
  input  i,
  input  Resetin,
  output Co,
  output [3:0] O,
  output bufferCLOCK
);

  wire and_3_out, and_4_out, clock_1_out, j_k_ff_1_q, j_k_ff_2_q, j_k_ff_3_q, j_k_ff_4_q, or_1_out, t_ff_1_q;

  T_Flip_Flop t_ff_1 (.T(1'b1), .clk(i), .Q(t_ff_1_q), .reset(Resetin));  // open: Qn, preset
  Clock clock_1 (.out(clock_1_out));
  or or_1 (or_1_out, Resetin, Co);
  and and_1 (bufferCLOCK, t_ff_1_q, clock_1_out);
  and and_2 (Co, j_k_ff_3_q, j_k_ff_1_q);
  J_K_Flip_Flop j_k_ff_1 (
    .J(and_3_out), .K(and_3_out), .clk(bufferCLOCK), .Q(j_k_ff_1_q), .reset(or_1_out));  // open: Qn, preset
  and and_3 (and_3_out, j_k_ff_4_q, j_k_ff_3_q, j_k_ff_2_q);
  LED led_1 (.in(j_k_ff_1_q));
  D_Flip_Flop d_ff_1 (.D(j_k_ff_1_q), .clk(bufferCLOCK), .Q(O[3]), .reset(Resetin));  // open: Qn, preset
  J_K_Flip_Flop j_k_ff_2 (
    .J(and_4_out), .K(and_4_out), .clk(bufferCLOCK), .Q(j_k_ff_2_q), .reset(or_1_out));  // open: Qn, preset
  and and_4 (and_4_out, j_k_ff_4_q, j_k_ff_3_q);
  LED led_2 (.in(j_k_ff_2_q));
  D_Flip_Flop d_ff_2 (.D(j_k_ff_2_q), .clk(bufferCLOCK), .Q(O[2]), .reset(Resetin));  // open: Qn, preset
  J_K_Flip_Flop j_k_ff_3 (
    .J(j_k_ff_4_q), .K(j_k_ff_4_q), .clk(bufferCLOCK), .Q(j_k_ff_3_q), .reset(or_1_out));  // open: Qn, preset
  LED led_3 (.in(j_k_ff_3_q));
  D_Flip_Flop d_ff_3 (.D(j_k_ff_3_q), .clk(bufferCLOCK), .Q(O[1]), .reset(Resetin));  // open: Qn, preset
  J_K_Flip_Flop j_k_ff_4 (.J(1'b1), .K(1'b1), .clk(bufferCLOCK), .Q(j_k_ff_4_q), .reset(or_1_out));  // open: Qn, preset
  LED led_4 (.in(j_k_ff_4_q));
  D_Flip_Flop d_ff_4 (.D(j_k_ff_4_q), .clk(bufferCLOCK), .Q(O[0]), .reset(Resetin));  // open: Qn, preset

  // Notes on the sheet:
  //   8
  //   4
  //   2
  //   1
endmodule

module subcircuit_stage3 (
  input  Ci,
  input  bufferCLOCK,
  input  Resetin,
  output Co,
  output [3:0] O
);

  wire and_2_out, j_k_ff_1_q, j_k_ff_2_q, j_k_ff_3_q, or_1_out;

  and and_1 (Co, j_k_ff_2_q, j_k_ff_1_q);
  or or_1 (or_1_out, Co, Resetin);
  and and_2 (and_2_out, j_k_ff_3_q, j_k_ff_2_q);
  J_K_Flip_Flop j_k_ff_1 (
    .J(and_2_out), .K(and_2_out), .clk(Ci), .Q(j_k_ff_1_q), .reset(or_1_out));  // open: Qn, preset
  J_K_Flip_Flop j_k_ff_2 (
    .J(j_k_ff_3_q), .K(j_k_ff_3_q), .clk(Ci), .Q(j_k_ff_2_q), .reset(or_1_out));  // open: Qn, preset
  LED led_1 (.in(j_k_ff_1_q));
  D_Flip_Flop d_ff_1 (.D(j_k_ff_1_q), .clk(bufferCLOCK), .Q(O[2]), .reset(Resetin));  // open: Qn, preset
  LED led_2 (.in(j_k_ff_2_q));
  J_K_Flip_Flop j_k_ff_3 (.J(1'b1), .K(1'b1), .clk(Ci), .Q(j_k_ff_3_q), .reset(or_1_out));  // open: Qn, preset
  D_Flip_Flop d_ff_2 (.D(j_k_ff_2_q), .clk(bufferCLOCK), .Q(O[1]), .reset(Resetin));  // open: Qn, preset
  LED led_3 (.in(j_k_ff_3_q));
  D_Flip_Flop d_ff_3 (.D(j_k_ff_3_q), .clk(bufferCLOCK), .Q(O[0]), .reset(Resetin));  // open: Qn, preset

  assign O[3] = 1'b0;

  // Notes on the sheet:
  //   4
  //   2
  //   1
endmodule

module subcircuit_stage4 (
  input  Ci,
  input  bufferCLOCK,
  input  Resetin,
  output [3:0] ones,
  output [3:0] tens
);

  wire and_1_out, and_2_out, and_3_out, and_4_out, and_5_out, and_6_out, j_k_ff_1_q, j_k_ff_2_q, j_k_ff_3_q,
       j_k_ff_4_q, j_k_ff_5_q, j_k_ff_6_q, j_k_ff_7_q, j_k_ff_8_q, or_1_out, or_2_out;

  or or_1 (or_1_out, Resetin, and_1_out);
  and and_1 (and_1_out, j_k_ff_3_q, j_k_ff_1_q);
  J_K_Flip_Flop j_k_ff_1 (
    .J(and_2_out), .K(and_2_out), .clk(Ci), .Q(j_k_ff_1_q), .reset(or_1_out));  // open: Qn, preset
  and and_2 (and_2_out, j_k_ff_4_q, j_k_ff_3_q, j_k_ff_2_q);
  LED led_1 (.in(j_k_ff_1_q));
  D_Flip_Flop d_ff_1 (.D(j_k_ff_1_q), .clk(bufferCLOCK), .Q(ones[3]), .reset(Resetin));  // open: Qn, preset
  J_K_Flip_Flop j_k_ff_2 (
    .J(and_3_out), .K(and_3_out), .clk(Ci), .Q(j_k_ff_2_q), .reset(or_1_out));  // open: Qn, preset
  and and_3 (and_3_out, j_k_ff_4_q, j_k_ff_3_q);
  LED led_2 (.in(j_k_ff_2_q));
  D_Flip_Flop d_ff_2 (.D(j_k_ff_2_q), .clk(bufferCLOCK), .Q(ones[2]), .reset(Resetin));  // open: Qn, preset
  J_K_Flip_Flop j_k_ff_3 (
    .J(j_k_ff_4_q), .K(j_k_ff_4_q), .clk(Ci), .Q(j_k_ff_3_q), .reset(or_1_out));  // open: Qn, preset
  LED led_3 (.in(j_k_ff_3_q));
  D_Flip_Flop d_ff_3 (.D(j_k_ff_3_q), .clk(bufferCLOCK), .Q(ones[1]), .reset(Resetin));  // open: Qn, preset
  J_K_Flip_Flop j_k_ff_4 (.J(1'b1), .K(1'b1), .clk(Ci), .Q(j_k_ff_4_q), .reset(or_1_out));  // open: Qn, preset
  LED led_4 (.in(j_k_ff_4_q));
  D_Flip_Flop d_ff_4 (.D(j_k_ff_4_q), .clk(bufferCLOCK), .Q(ones[0]), .reset(Resetin));  // open: Qn, preset
  and and_4 (and_4_out, j_k_ff_7_q, j_k_ff_5_q);
  or or_2 (or_2_out, Resetin, and_4_out);
  and and_5 (and_5_out, j_k_ff_8_q, j_k_ff_7_q, j_k_ff_6_q);
  J_K_Flip_Flop j_k_ff_5 (
    .J(and_5_out), .K(and_5_out), .clk(and_1_out), .Q(j_k_ff_5_q), .reset(or_2_out));  // open: Qn, preset
  LED led_5 (.in(j_k_ff_5_q));
  D_Flip_Flop d_ff_5 (.D(j_k_ff_5_q), .clk(bufferCLOCK), .Q(tens[3]), .reset(Resetin));  // open: Qn, preset
  J_K_Flip_Flop j_k_ff_6 (
    .J(and_6_out), .K(and_6_out), .clk(and_1_out), .Q(j_k_ff_6_q), .reset(or_2_out));  // open: Qn, preset
  and and_6 (and_6_out, j_k_ff_8_q, j_k_ff_7_q);
  LED led_6 (.in(j_k_ff_6_q));
  D_Flip_Flop d_ff_6 (.D(j_k_ff_6_q), .clk(bufferCLOCK), .Q(tens[2]), .reset(Resetin));  // open: Qn, preset
  J_K_Flip_Flop j_k_ff_7 (
    .J(j_k_ff_8_q), .K(j_k_ff_8_q), .clk(and_1_out), .Q(j_k_ff_7_q), .reset(or_2_out));  // open: Qn, preset
  LED led_7 (.in(j_k_ff_7_q));
  D_Flip_Flop d_ff_7 (.D(j_k_ff_7_q), .clk(bufferCLOCK), .Q(tens[1]), .reset(Resetin));  // open: Qn, preset
  J_K_Flip_Flop j_k_ff_8 (.J(1'b1), .K(1'b1), .clk(and_1_out), .Q(j_k_ff_8_q), .reset(or_2_out));  // open: Qn, preset
  LED led_8 (.in(j_k_ff_8_q));
  D_Flip_Flop d_ff_8 (.D(j_k_ff_8_q), .clk(bufferCLOCK), .Q(tens[0]), .reset(Resetin));  // open: Qn, preset

  // Notes on the sheet:
  //   8
  //   4
  //   2
  //   1
  //   8
  //   4
  //   2
  //   1
endmodule
