// Logisim project stage6.circ as structural Verilog: 8 circuits, main circuit main
module main (
);

  wire button_1_out, button_2_out, button_3_out, subcircuit_stage1_1_onoff, subcircuit_stage2_1_bufferclock,
       subcircuit_stage2_1_co, subcircuit_stage3_1_co;
  wire [3:0] myencoder_1_mainout, myencoder_2_mainout, myencoder_3_mainout, myencoder_4_mainout,
       myselector_1_o, myselector_2_o, myselector_3_o, myselector_4_o, subcircuit_stage2_1_o,
       subcircuit_stage3_1_o, subcircuit_stage4_1_ones, subcircuit_stage4_1_tens,
       subcircuit_stage6_1_splitout0, subcircuit_stage6_1_splitout1, subcircuit_stage6_1_splitout2,
       subcircuit_stage6_1_splitout3, subcircuit_stage6_1_splitout4, subcircuit_stage6_2_splitout0,
       subcircuit_stage6_2_splitout1, subcircuit_stage6_2_splitout2, subcircuit_stage6_2_splitout3,
       subcircuit_stage6_2_splitout4, subcircuit_stage6_3_splitout0, subcircuit_stage6_3_splitout1,
       subcircuit_stage6_3_splitout2, subcircuit_stage6_3_splitout3, subcircuit_stage6_3_splitout4,
       subcircuit_stage6_4_splitout0, subcircuit_stage6_4_splitout1, subcircuit_stage6_4_splitout2,
       subcircuit_stage6_4_splitout3, subcircuit_stage6_4_splitout4;

  Button button_1 (.out(button_1_out));
  Hex_Digit_Display hex_digit_display_1 (.value(subcircuit_stage4_1_tens));  // open: dp
  Hex_Digit_Display hex_digit_display_2 (.value(subcircuit_stage4_1_ones));  // open: dp
  Hex_Digit_Display hex_digit_display_3 (.value(subcircuit_stage3_1_o));  // open: dp
  Hex_Digit_Display hex_digit_display_4 (.value(subcircuit_stage2_1_o));  // open: dp
  Button button_2 (.out(button_2_out));
  Button button_3 (.out(button_3_out));
  subcircuit_stage1 subcircuit_stage1_1 (.i(button_1_out), .Resetin(button_3_out), .onOFF(subcircuit_stage1_1_onoff));
  subcircuit_stage2 subcircuit_stage2_1 (
    .i(button_1_out), .Resetin(button_3_out), .Co(subcircuit_stage2_1_co), .O(subcircuit_stage2_1_o),
    .bufferCLOCK(subcircuit_stage2_1_bufferclock));
  subcircuit_stage3 subcircuit_stage3_1 (
    .Ci(subcircuit_stage2_1_co), .bufferCLOCK(subcircuit_stage2_1_bufferclock), .Resetin(button_3_out),
    .Co(subcircuit_stage3_1_co), .O(subcircuit_stage3_1_o));
  subcircuit_stage4 subcircuit_stage4_1 (
    .Ci(subcircuit_stage3_1_co), .bufferCLOCK(subcircuit_stage2_1_bufferclock), .Resetin(button_3_out),
    .ones(subcircuit_stage4_1_ones), .tens(subcircuit_stage4_1_tens));
  Hex_Digit_Display hex_digit_display_5 (.value(myselector_3_o));  // open: dp
  LED led_1 (.in(subcircuit_stage1_1_onoff));
  Hex_Digit_Display hex_digit_display_6 (.value(myselector_4_o));  // open: dp
  Hex_Digit_Display hex_digit_display_7 (.value(myselector_2_o));  // open: dp
  Hex_Digit_Display hex_digit_display_8 (.value(myselector_1_o));  // open: dp
  subcircuit_stage6 subcircuit_stage6_1 (
    .ONoff(subcircuit_stage1_1_onoff), .splitIN(button_2_out), .resetIN(button_3_out),
    .i0(subcircuit_stage2_1_o[0]), .i1(subcircuit_stage2_1_o[1]), .i2(subcircuit_stage2_1_o[2]),
    .i3(subcircuit_stage2_1_o[3]), .splitOUT0(subcircuit_stage6_1_splitout0),
    .splitOUT1(subcircuit_stage6_1_splitout1), .splitOUT2(subcircuit_stage6_1_splitout2),
    .splitOUT3(subcircuit_stage6_1_splitout3), .splitOUT4(subcircuit_stage6_1_splitout4));
  subcircuit_stage6 subcircuit_stage6_2 (
    .ONoff(subcircuit_stage1_1_onoff), .splitIN(button_2_out), .resetIN(button_3_out),
    .i0(subcircuit_stage3_1_o[0]), .i1(subcircuit_stage3_1_o[1]), .i2(subcircuit_stage3_1_o[2]),
    .i3(subcircuit_stage3_1_o[3]), .splitOUT0(subcircuit_stage6_2_splitout0),
    .splitOUT1(subcircuit_stage6_2_splitout1), .splitOUT2(subcircuit_stage6_2_splitout2),
    .splitOUT3(subcircuit_stage6_2_splitout3), .splitOUT4(subcircuit_stage6_2_splitout4));
  subcircuit_stage6 subcircuit_stage6_3 (
    .ONoff(subcircuit_stage1_1_onoff), .splitIN(button_2_out), .resetIN(button_3_out),
    .i0(subcircuit_stage4_1_tens[0]), .i1(subcircuit_stage4_1_tens[1]), .i2(subcircuit_stage4_1_tens[2]),
    .i3(subcircuit_stage4_1_tens[3]), .splitOUT0(subcircuit_stage6_3_splitout0),
    .splitOUT1(subcircuit_stage6_3_splitout1), .splitOUT2(subcircuit_stage6_3_splitout2),
    .splitOUT3(subcircuit_stage6_3_splitout3), .splitOUT4(subcircuit_stage6_3_splitout4));
  subcircuit_stage6 subcircuit_stage6_4 (
    .ONoff(subcircuit_stage1_1_onoff), .splitIN(button_2_out), .resetIN(button_3_out),
    .i0(subcircuit_stage4_1_ones[0]), .i1(subcircuit_stage4_1_ones[1]), .i2(subcircuit_stage4_1_ones[2]),
    .i3(subcircuit_stage4_1_ones[3]), .splitOUT0(subcircuit_stage6_4_splitout0),
    .splitOUT1(subcircuit_stage6_4_splitout1), .splitOUT2(subcircuit_stage6_4_splitout2),
    .splitOUT3(subcircuit_stage6_4_splitout3), .splitOUT4(subcircuit_stage6_4_splitout4));
  Hex_Digit_Display hex_digit_display_9 (.value(subcircuit_stage6_3_splitout0));  // open: dp
  Hex_Digit_Display hex_digit_display_10 (.value(subcircuit_stage6_3_splitout1));  // open: dp
  Hex_Digit_Display hex_digit_display_11 (.value(subcircuit_stage6_3_splitout2));  // open: dp
  Hex_Digit_Display hex_digit_display_12 (.value(subcircuit_stage6_3_splitout3));  // open: dp
  Hex_Digit_Display hex_digit_display_13 (.value(subcircuit_stage6_3_splitout4));  // open: dp
  Hex_Digit_Display hex_digit_display_14 (.value(subcircuit_stage6_4_splitout0));  // open: dp
  Hex_Digit_Display hex_digit_display_15 (.value(subcircuit_stage6_4_splitout1));  // open: dp
  Hex_Digit_Display hex_digit_display_16 (.value(subcircuit_stage6_4_splitout2));  // open: dp
  Hex_Digit_Display hex_digit_display_17 (.value(subcircuit_stage6_4_splitout3));  // open: dp
  Hex_Digit_Display hex_digit_display_18 (.value(subcircuit_stage6_4_splitout4));  // open: dp
  Hex_Digit_Display hex_digit_display_19 (.value(subcircuit_stage6_2_splitout0));  // open: dp
  Hex_Digit_Display hex_digit_display_20 (.value(subcircuit_stage6_1_splitout0));  // open: dp
  Hex_Digit_Display hex_digit_display_21 (.value(subcircuit_stage6_2_splitout1));  // open: dp
  Hex_Digit_Display hex_digit_display_22 (.value(subcircuit_stage6_2_splitout2));  // open: dp
  Hex_Digit_Display hex_digit_display_23 (.value(subcircuit_stage6_2_splitout3));  // open: dp
  Hex_Digit_Display hex_digit_display_24 (.value(subcircuit_stage6_2_splitout4));  // open: dp
  Hex_Digit_Display hex_digit_display_25 (.value(subcircuit_stage6_1_splitout1));  // open: dp
  Hex_Digit_Display hex_digit_display_26 (.value(subcircuit_stage6_1_splitout2));  // open: dp
  Hex_Digit_Display hex_digit_display_27 (.value(subcircuit_stage6_1_splitout3));  // open: dp
  Hex_Digit_Display hex_digit_display_28 (.value(subcircuit_stage6_1_splitout4));  // open: dp
  myEncoder myencoder_1 (
    .onOFF(subcircuit_stage1_1_onoff), .splitIN(button_2_out), .resetIN(button_3_out),
    .splitIN0(subcircuit_stage6_1_splitout0), .splitIN1(subcircuit_stage6_1_splitout1),
    .splitIN2(subcircuit_stage6_1_splitout2), .splitIN3(subcircuit_stage6_1_splitout3),
    .splitIN4(subcircuit_stage6_1_splitout4), .mainOUT(myencoder_1_mainout));
  myEncoder myencoder_2 (
    .onOFF(subcircuit_stage1_1_onoff), .splitIN(button_2_out), .resetIN(button_3_out),
    .splitIN0(subcircuit_stage6_2_splitout0), .splitIN1(subcircuit_stage6_2_splitout1),
    .splitIN2(subcircuit_stage6_2_splitout2), .splitIN3(subcircuit_stage6_2_splitout3),
    .splitIN4(subcircuit_stage6_2_splitout4), .mainOUT(myencoder_2_mainout));
  myEncoder myencoder_3 (
    .onOFF(subcircuit_stage1_1_onoff), .splitIN(button_2_out), .resetIN(button_3_out),
    .splitIN0(subcircuit_stage6_3_splitout0), .splitIN1(subcircuit_stage6_3_splitout1),
    .splitIN2(subcircuit_stage6_3_splitout2), .splitIN3(subcircuit_stage6_3_splitout3),
    .splitIN4(subcircuit_stage6_3_splitout4), .mainOUT(myencoder_3_mainout));
  myEncoder myencoder_4 (
    .onOFF(subcircuit_stage1_1_onoff), .splitIN(button_2_out), .resetIN(button_3_out),
    .splitIN0(subcircuit_stage6_4_splitout0), .splitIN1(subcircuit_stage6_4_splitout1),
    .splitIN2(subcircuit_stage6_4_splitout2), .splitIN3(subcircuit_stage6_4_splitout3),
    .splitIN4(subcircuit_stage6_4_splitout4), .mainOUT(myencoder_4_mainout));
  mySelector myselector_1 (
    .ONoff(subcircuit_stage1_1_onoff), .splitIN(myencoder_1_mainout),
    .elapsedIN(subcircuit_stage6_1_splitout0), .O(myselector_1_o));
  mySelector myselector_2 (
    .ONoff(subcircuit_stage1_1_onoff), .splitIN(myencoder_2_mainout),
    .elapsedIN(subcircuit_stage6_2_splitout0), .O(myselector_2_o));
  mySelector myselector_3 (
    .ONoff(subcircuit_stage1_1_onoff), .splitIN(myencoder_3_mainout),
    .elapsedIN(subcircuit_stage6_3_splitout0), .O(myselector_3_o));
  mySelector myselector_4 (
    .ONoff(subcircuit_stage1_1_onoff), .splitIN(myencoder_4_mainout),
    .elapsedIN(subcircuit_stage6_4_splitout0), .O(myselector_4_o));

  // Notes on the sheet:
  //   Start / Stop
  //   Elapsed Time
  //   Minutes
  //   :
  //   Seconds
  //   Split
  //   Reset
  //   Clock Started
  //   Split Time
  //   Minutes
  //   :
  //   Seconds
  //   Ones place of the seconds counter for split display
  //   Tens place of the seconds counter for split display
  //   Tens place of the minutes counter for split display
  //   Ones place of the minutes counter for split display
  //   Recorded Split Times
  //   Minutes
  //   :
  //   Seconds
  //   :
  //   :
  //   :
  //   :
endmodule

module subcircuit_stage1 (
  input  i,
  input  Resetin,
  output onOFF
);

  T_Flip_Flop t_ff_1 (.T(1'b1), .clk(i), .Q(onOFF), .reset(Resetin));  // open: Qn, preset
endmodule

module subcircuit_stage2 (
  input  i,
  input  Resetin,
  output Co,
  output [3:0] O,
  output bufferCLOCK
);

  wire and_2_out, and_3_out, and_4_out, clock_1_out, j_k_ff_1_q, j_k_ff_2_q, j_k_ff_3_q, j_k_ff_4_q, t_ff_1_q;

  T_Flip_Flop t_ff_1 (.T(1'b1), .clk(i), .Q(t_ff_1_q), .reset(Resetin));  // open: Qn, preset
  Clock clock_1 (.out(clock_1_out));
  or or_1 (Co, Resetin, and_2_out);
  and and_1 (bufferCLOCK, t_ff_1_q, clock_1_out);
  and and_2 (and_2_out, j_k_ff_3_q, j_k_ff_1_q);
  J_K_Flip_Flop j_k_ff_1 (
    .J(and_3_out), .K(and_3_out), .clk(bufferCLOCK), .Q(j_k_ff_1_q), .reset(Co));  // open: Qn, preset
  and and_3 (and_3_out, j_k_ff_4_q, j_k_ff_3_q, j_k_ff_2_q);
  LED led_1 (.in(j_k_ff_1_q));
  D_Flip_Flop d_ff_1 (.D(j_k_ff_1_q), .clk(bufferCLOCK), .Q(O[3]), .reset(Resetin));  // open: Qn, preset
  J_K_Flip_Flop j_k_ff_2 (
    .J(and_4_out), .K(and_4_out), .clk(bufferCLOCK), .Q(j_k_ff_2_q), .reset(Co));  // open: Qn, preset
  and and_4 (and_4_out, j_k_ff_4_q, j_k_ff_3_q);
  LED led_2 (.in(j_k_ff_2_q));
  D_Flip_Flop d_ff_2 (.D(j_k_ff_2_q), .clk(bufferCLOCK), .Q(O[2]), .reset(Resetin));  // open: Qn, preset
  J_K_Flip_Flop j_k_ff_3 (
    .J(j_k_ff_4_q), .K(j_k_ff_4_q), .clk(bufferCLOCK), .Q(j_k_ff_3_q), .reset(Co));  // open: Qn, preset
  LED led_3 (.in(j_k_ff_3_q));
  D_Flip_Flop d_ff_3 (.D(j_k_ff_3_q), .clk(bufferCLOCK), .Q(O[1]), .reset(Resetin));  // open: Qn, preset
  J_K_Flip_Flop j_k_ff_4 (.J(1'b1), .K(1'b1), .clk(bufferCLOCK), .Q(j_k_ff_4_q), .reset(Co));  // open: Qn, preset
  LED led_4 (.in(j_k_ff_4_q));
  D_Flip_Flop d_ff_4 (.D(j_k_ff_4_q), .clk(bufferCLOCK), .Q(O[0]), .reset(Resetin));  // open: Qn, preset

  // Notes on the sheet:
  //   8
  //   4
  //   2
  //   1
endmodule

module subcircuit_stage3 (
  input  Ci,
  input  bufferCLOCK,
  input  Resetin,
  output Co,
  output [3:0] O
);

  wire and_2_out, j_k_ff_1_q, j_k_ff_2_q, j_k_ff_3_q, or_1_out;

  and and_1 (Co, j_k_ff_2_q, j_k_ff_1_q);
  or or_1 (or_1_out, Co, Resetin);
  J_K_Flip_Flop j_k_ff_1 (
    .J(and_2_out), .K(and_2_out), .clk(Ci), .Q(j_k_ff_1_q), .reset(or_1_out));  // open: Qn, preset
  and and_2 (and_2_out, j_k_ff_3_q, j_k_ff_2_q);
  LED led_1 (.in(j_k_ff_1_q));
  J_K_Flip_Flop j_k_ff_2 (
    .J(j_k_ff_3_q), .K(j_k_ff_3_q), .clk(Ci), .Q(j_k_ff_2_q), .reset(or_1_out));  // open: Qn, preset
  D_Flip_Flop d_ff_1 (.D(j_k_ff_1_q), .clk(bufferCLOCK), .Q(O[2]), .reset(Resetin));  // open: Qn, preset
  J_K_Flip_Flop j_k_ff_3 (.J(1'b1), .K(1'b1), .clk(Ci), .Q(j_k_ff_3_q), .reset(or_1_out));  // open: Qn, preset
  LED led_2 (.in(j_k_ff_2_q));
  D_Flip_Flop d_ff_2 (.D(j_k_ff_2_q), .clk(bufferCLOCK), .Q(O[1]), .reset(Resetin));  // open: Qn, preset
  LED led_3 (.in(j_k_ff_3_q));
  D_Flip_Flop d_ff_3 (.D(j_k_ff_3_q), .clk(bufferCLOCK), .Q(O[0]), .reset(Resetin));  // open: Qn, preset

  assign O[3] = 1'b0;

  // Notes on the sheet:
  //   4
  //   2
  //   1
endmodule

module subcircuit_stage4 (
  input  Ci,
  input  bufferCLOCK,
  input  Resetin,
  output [3:0] ones,
  output [3:0] tens
);

  wire and_1_out, and_2_out, and_3_out, and_4_out, and_5_out, and_6_out, j_k_ff_1_q, j_k_ff_2_q, j_k_ff_3_q,
       j_k_ff_4_q, j_k_ff_5_q, j_k_ff_6_q, j_k_ff_7_q, j_k_ff_8_q, or_1_out, or_2_out;

  or or_1 (or_1_out, Resetin, and_1_out);
  and and_1 (and_1_out, j_k_ff_3_q, j_k_ff_1_q);
  J_K_Flip_Flop j_k_ff_1 (
    .J(and_2_out), .K(and_2_out), .clk(Ci), .Q(j_k_ff_1_q), .reset(or_1_out));  // open: Qn, preset
  and and_2 (and_2_out, j_k_ff_4_q, j_k_ff_3_q, j_k_ff_2_q);
  LED led_1 (.in(j_k_ff_1_q));
  D_Flip_Flop d_ff_1 (.D(j_k_ff_1_q), .clk(bufferCLOCK), .Q(ones[3]), .reset(Resetin));  // open: Qn, preset
  J_K_Flip_Flop j_k_ff_2 (
    .J(and_3_out), .K(and_3_out), .clk(Ci), .Q(j_k_ff_2_q), .reset(or_1_out));  // open: Qn, preset
  and and_3 (and_3_out, j_k_ff_4_q, j_k_ff_3_q);
  LED led_2 (.in(j_k_ff_2_q));
  D_Flip_Flop d_ff_2 (.D(j_k_ff_2_q), .clk(bufferCLOCK), .Q(ones[2]), .reset(Resetin));  // open: Qn, preset
  J_K_Flip_Flop j_k_ff_3 (
    .J(j_k_ff_4_q), .K(j_k_ff_4_q), .clk(Ci), .Q(j_k_ff_3_q), .reset(or_1_out));  // open: Qn, preset
  LED led_3 (.in(j_k_ff_3_q));
  D_Flip_Flop d_ff_3 (.D(j_k_ff_3_q), .clk(bufferCLOCK), .Q(ones[1]), .reset(Resetin));  // open: Qn, preset
  J_K_Flip_Flop j_k_ff_4 (.J(1'b1), .K(1'b1), .clk(Ci), .Q(j_k_ff_4_q), .reset(or_1_out));  // open: Qn, preset
  LED led_4 (.in(j_k_ff_4_q));
  D_Flip_Flop d_ff_4 (.D(j_k_ff_4_q), .clk(bufferCLOCK), .Q(ones[0]), .reset(Resetin));  // open: Qn, preset
  and and_4 (and_4_out, j_k_ff_7_q, j_k_ff_5_q);
  or or_2 (or_2_out, Resetin, and_4_out);
  and and_5 (and_5_out, j_k_ff_8_q, j_k_ff_7_q, j_k_ff_6_q);
  J_K_Flip_Flop j_k_ff_5 (
    .J(and_5_out), .K(and_5_out), .clk(and_1_out), .Q(j_k_ff_5_q), .reset(or_2_out));  // open: Qn, preset
  LED led_5 (.in(j_k_ff_5_q));
  D_Flip_Flop d_ff_5 (.D(j_k_ff_5_q), .clk(bufferCLOCK), .Q(tens[3]), .reset(Resetin));  // open: Qn, preset
  J_K_Flip_Flop j_k_ff_6 (
    .J(and_6_out), .K(and_6_out), .clk(and_1_out), .Q(j_k_ff_6_q), .reset(or_2_out));  // open: Qn, preset
  and and_6 (and_6_out, j_k_ff_8_q, j_k_ff_7_q);
  LED led_6 (.in(j_k_ff_6_q));
  D_Flip_Flop d_ff_6 (.D(j_k_ff_6_q), .clk(bufferCLOCK), .Q(tens[2]), .reset(Resetin));  // open: Qn, preset
  J_K_Flip_Flop j_k_ff_7 (
    .J(j_k_ff_8_q), .K(j_k_ff_8_q), .clk(and_1_out), .Q(j_k_ff_7_q), .reset(or_2_out));  // open: Qn, preset
  LED led_7 (.in(j_k_ff_7_q));
  D_Flip_Flop d_ff_7 (.D(j_k_ff_7_q), .clk(bufferCLOCK), .Q(tens[1]), .reset(Resetin));  // open: Qn, preset
  J_K_Flip_Flop j_k_ff_8 (.J(1'b1), .K(1'b1), .clk(and_1_out), .Q(j_k_ff_8_q), .reset(or_2_out));  // open: Qn, preset
  LED led_8 (.in(j_k_ff_8_q));
  D_Flip_Flop d_ff_8 (.D(j_k_ff_8_q), .clk(bufferCLOCK), .Q(tens[0]), .reset(Resetin));  // open: Qn, preset

  // Notes on the sheet:
  //   8
  //   4
  //   2
  //   1
  //   8
  //   4
  //   2
  //   1
endmodule

module subcircuit_stage6 (
  input  ONoff,
  input  splitIN,
  input  resetIN,
  input  i0,
  input  i1,
  input  i2,
  input  i3,
  output [3:0] splitOUT0,
  output [3:0] splitOUT1,
  output [3:0] splitOUT2,
  output [3:0] splitOUT3,
  output [3:0] splitOUT4
);

  wire and_1_out, and_2_out, and_3_out, and_4_out, and_5_out, and_6_out, and_7_out, and_8_out, and_9_out,
       and_10_out, and_11_out, and_12_out, and_13_out, and_14_out, and_15_out, and_16_out, and_17_out,
       and_18_out, and_19_out, and_20_out, and_21_out, and_22_out, and_23_out, and_24_out, and_25_out,
       and_26_out, and_27_out, and_28_out, and_29_out, and_30_out, and_31_out, and_32_out, and_33_out,
       and_34_out, and_35_out, and_36_out, and_37_out, and_38_out, and_39_out, and_40_out, and_41_out,
       and_42_out, clock_1_out, d_ff_1_q, d_ff_2_q, d_ff_3_q, d_ff_4_q, d_ff_5_q, d_ff_6_q, d_ff_7_q,
       d_ff_8_q, d_ff_9_q, d_ff_10_q, d_ff_11_q, d_ff_12_q, d_ff_13_q, d_ff_14_q, d_ff_15_q, d_ff_16_q,
       d_ff_17_q, d_ff_18_q, d_ff_19_q, d_ff_20_q, d_ff_21_q, d_ff_22_q, d_ff_23_q, d_ff_24_q, d_ff_25_q,
       d_ff_26_q, d_ff_27_q, d_ff_28_q, d_ff_29_q, d_ff_30_q, d_ff_31_q, d_ff_32_q, d_ff_33_q, d_ff_34_q,
       d_ff_35_q, d_ff_36_q, d_ff_37_q, d_ff_38_q, d_ff_40_q, d_ff_43_q, not_1_out, not_2_out, not_3_out,
       not_4_out, not_5_out, or_1_out, or_2_out, or_3_out, or_4_out, or_5_out, or_6_out, or_7_out, or_8_out,
       or_9_out, or_10_out, or_11_out, or_12_out, or_13_out, or_14_out, or_15_out, or_16_out, or_17_out,
       or_18_out, or_19_out, or_20_out;

  not not_1 (not_1_out, ONoff);
  and and_1 (and_1_out, splitIN, ONoff);
  not not_2 (not_2_out, and_1_out);
  Clock clock_1 (.out(clock_1_out));
  and and_2 (and_2_out, not_2_out, clock_1_out);
  and and_3 (and_3_out, ONoff, i0);
  or or_1 (or_1_out, and_3_out, and_4_out);
  D_Flip_Flop d_ff_1 (.D(or_1_out), .clk(and_1_out), .Q(d_ff_1_q), .reset(resetIN));  // open: Qn, preset
  and and_4 (and_4_out, not_1_out, d_ff_6_q);
  not not_3 (not_3_out, ONoff);
  and and_5 (and_5_out, ONoff, i1);
  not not_4 (not_4_out, ONoff);
  and and_6 (and_6_out, ONoff, i2);
  not not_5 (not_5_out, ONoff);
  and and_7 (and_7_out, ONoff, i3);
  and and_8 (and_8_out, ONoff, d_ff_1_q);
  LED led_1 (.in(d_ff_1_q));
  D_Flip_Flop d_ff_2 (.D(d_ff_1_q), .clk(and_2_out), .Q(d_ff_2_q), .reset(resetIN));  // open: Qn, preset
  and and_9 (and_9_out, not_3_out, d_ff_11_q);
  or or_2 (or_2_out, and_5_out, and_9_out);
  D_Flip_Flop d_ff_3 (.D(or_2_out), .clk(and_1_out), .Q(d_ff_3_q), .reset(resetIN));  // open: Qn, preset
  and and_10 (and_10_out, not_4_out, d_ff_12_q);
  or or_3 (or_3_out, and_6_out, and_10_out);
  D_Flip_Flop d_ff_4 (.D(or_3_out), .clk(and_1_out), .Q(d_ff_4_q), .reset(resetIN));  // open: Qn, preset
  and and_11 (and_11_out, not_5_out, d_ff_13_q);
  or or_4 (or_4_out, and_7_out, and_11_out);
  D_Flip_Flop d_ff_5 (.D(or_4_out), .clk(and_1_out), .Q(d_ff_5_q), .reset(resetIN));  // open: Qn, preset
  and and_12 (and_12_out, not_1_out, d_ff_14_q);
  or or_5 (or_5_out, and_8_out, and_12_out);
  D_Flip_Flop d_ff_6 (.D(or_5_out), .clk(and_1_out), .Q(d_ff_6_q), .reset(resetIN));  // open: Qn, preset
  LED led_2 (.in(d_ff_2_q));
  LED led_3 (.in(d_ff_3_q));
  D_Flip_Flop d_ff_7 (.D(d_ff_3_q), .clk(and_2_out), .Q(d_ff_7_q), .reset(resetIN));  // open: Qn, preset
  D_Flip_Flop d_ff_8 (.D(d_ff_4_q), .clk(and_2_out), .Q(d_ff_8_q), .reset(resetIN));  // open: Qn, preset
  D_Flip_Flop d_ff_9 (.D(d_ff_5_q), .clk(and_2_out), .Q(d_ff_9_q), .reset(resetIN));  // open: Qn, preset
  and and_13 (and_13_out, ONoff, d_ff_6_q);
  LED led_4 (.in(d_ff_6_q));
  D_Flip_Flop d_ff_10 (.D(d_ff_6_q), .clk(and_2_out), .Q(d_ff_10_q), .reset(resetIN));  // open: Qn, preset
  and and_14 (and_14_out, ONoff, d_ff_3_q);
  and and_15 (and_15_out, not_3_out, d_ff_18_q);
  or or_6 (or_6_out, and_14_out, and_15_out);
  D_Flip_Flop d_ff_11 (.D(or_6_out), .clk(and_1_out), .Q(d_ff_11_q), .reset(resetIN));  // open: Qn, preset
  LED led_5 (.in(d_ff_7_q));
  and and_16 (and_16_out, ONoff, d_ff_4_q);
  or or_7 (or_7_out, and_16_out, and_20_out);
  D_Flip_Flop d_ff_12 (.D(or_7_out), .clk(and_1_out), .Q(d_ff_12_q), .reset(resetIN));  // open: Qn, preset
  LED led_6 (.in(d_ff_4_q));
  LED led_7 (.in(d_ff_8_q));
  and and_17 (and_17_out, ONoff, d_ff_5_q);
  and and_18 (and_18_out, not_5_out, d_ff_20_q);
  or or_8 (or_8_out, and_17_out, and_18_out);
  D_Flip_Flop d_ff_13 (.D(or_8_out), .clk(and_1_out), .Q(d_ff_13_q), .reset(resetIN));  // open: Qn, preset
  LED led_8 (.in(d_ff_5_q));
  LED led_9 (.in(d_ff_9_q));
  and and_19 (and_19_out, not_1_out, d_ff_21_q);
  or or_9 (or_9_out, and_13_out, and_19_out);
  D_Flip_Flop d_ff_14 (.D(or_9_out), .clk(and_1_out), .Q(d_ff_14_q), .reset(resetIN));  // open: Qn, preset
  LED led_10 (.in(d_ff_10_q));
  LED led_11 (.in(d_ff_11_q));
  D_Flip_Flop d_ff_15 (.D(d_ff_11_q), .clk(and_2_out), .Q(d_ff_15_q), .reset(resetIN));  // open: Qn, preset
  and and_20 (and_20_out, not_4_out, d_ff_23_q);
  D_Flip_Flop d_ff_16 (.D(d_ff_13_q), .clk(and_2_out), .Q(d_ff_16_q), .reset(resetIN));  // open: Qn, preset
  and and_21 (and_21_out, ONoff, d_ff_14_q);
  LED led_12 (.in(d_ff_14_q));
  D_Flip_Flop d_ff_17 (.D(d_ff_14_q), .clk(and_2_out), .Q(d_ff_17_q), .reset(resetIN));  // open: Qn, preset
  and and_22 (and_22_out, ONoff, d_ff_11_q);
  and and_23 (and_23_out, not_3_out, d_ff_25_q);
  or or_10 (or_10_out, and_22_out, and_23_out);
  D_Flip_Flop d_ff_18 (.D(or_10_out), .clk(and_1_out), .Q(d_ff_18_q), .reset(resetIN));  // open: Qn, preset
  LED led_13 (.in(d_ff_15_q));
  and and_24 (and_24_out, ONoff, d_ff_12_q);
  or or_11 (or_11_out, and_24_out, and_27_out);
  LED led_14 (.in(d_ff_12_q));
  D_Flip_Flop d_ff_19 (.D(d_ff_12_q), .clk(and_2_out), .Q(d_ff_19_q), .reset(resetIN));  // open: Qn, preset
  LED led_15 (.in(d_ff_19_q));
  and and_25 (and_25_out, ONoff, d_ff_13_q);
  or or_12 (or_12_out, and_25_out, and_28_out);
  D_Flip_Flop d_ff_20 (.D(or_12_out), .clk(and_1_out), .Q(d_ff_20_q), .reset(resetIN));  // open: Qn, preset
  LED led_16 (.in(d_ff_13_q));
  LED led_17 (.in(d_ff_16_q));
  and and_26 (and_26_out, not_1_out, d_ff_28_q);
  or or_13 (or_13_out, and_21_out, and_26_out);
  D_Flip_Flop d_ff_21 (.D(or_13_out), .clk(and_1_out), .Q(d_ff_21_q), .reset(resetIN));  // open: Qn, preset
  LED led_18 (.in(d_ff_17_q));
  LED led_19 (.in(d_ff_18_q));
  D_Flip_Flop d_ff_22 (.D(d_ff_18_q), .clk(and_2_out), .Q(d_ff_22_q), .reset(resetIN));  // open: Qn, preset
  and and_27 (and_27_out, not_4_out, d_ff_30_q);
  D_Flip_Flop d_ff_23 (.D(or_11_out), .clk(and_1_out), .Q(d_ff_23_q), .reset(resetIN));  // open: Qn, preset
  and and_28 (and_28_out, not_5_out, d_ff_31_q);
  LED led_20 (.in(d_ff_21_q));
  D_Flip_Flop d_ff_24 (.D(d_ff_21_q), .clk(and_2_out), .Q(d_ff_24_q), .reset(resetIN));  // open: Qn, preset
  and and_29 (and_29_out, ONoff, d_ff_18_q);
  and and_30 (and_30_out, not_3_out, d_ff_35_q);
  or or_14 (or_14_out, and_29_out, and_30_out);
  D_Flip_Flop d_ff_25 (.D(or_14_out), .clk(and_1_out), .Q(d_ff_25_q), .reset(resetIN));  // open: Qn, preset
  LED led_21 (.in(d_ff_22_q));
  and and_31 (and_31_out, ONoff, d_ff_23_q);
  LED led_22 (.in(d_ff_23_q));
  D_Flip_Flop d_ff_26 (.D(d_ff_23_q), .clk(and_2_out), .Q(d_ff_26_q), .reset(resetIN));  // open: Qn, preset
  and and_32 (and_32_out, ONoff, d_ff_20_q);
  or or_15 (or_15_out, and_32_out, and_35_out);
  LED led_23 (.in(d_ff_20_q));
  D_Flip_Flop d_ff_27 (.D(d_ff_20_q), .clk(and_2_out), .Q(d_ff_27_q), .reset(resetIN));  // open: Qn, preset
  and and_33 (and_33_out, ONoff, d_ff_21_q);
  D_Flip_Flop d_ff_28 (.D(or_17_out), .clk(and_1_out), .Q(d_ff_28_q), .reset(resetIN));  // open: Qn, preset
  LED led_24 (.in(d_ff_24_q));
  D_Flip_Flop d_ff_29 (.D(d_ff_25_q), .clk(and_2_out), .Q(d_ff_29_q), .reset(resetIN));  // open: Qn, preset
  and and_34 (and_34_out, not_4_out, d_ff_36_q);
  or or_16 (or_16_out, and_31_out, and_34_out);
  D_Flip_Flop d_ff_30 (.D(or_16_out), .clk(and_1_out), .Q(d_ff_30_q), .reset(resetIN));  // open: Qn, preset
  LED led_25 (.in(d_ff_26_q));
  and and_35 (and_35_out, not_5_out, d_ff_37_q);
  D_Flip_Flop d_ff_31 (.D(or_15_out), .clk(and_1_out), .Q(d_ff_31_q), .reset(resetIN));  // open: Qn, preset
  LED led_26 (.in(d_ff_27_q));
  and and_36 (and_36_out, not_1_out, 1'b0);
  or or_17 (or_17_out, and_33_out, and_36_out);
  D_Flip_Flop d_ff_32 (.D(d_ff_28_q), .clk(and_2_out), .Q(d_ff_32_q), .reset(resetIN));  // open: Qn, preset
  and and_37 (and_37_out, ONoff, d_ff_25_q);
  LED led_27 (.in(d_ff_25_q));
  LED led_28 (.in(d_ff_29_q));
  LED led_29 (.in(d_ff_30_q));
  D_Flip_Flop d_ff_33 (.D(d_ff_30_q), .clk(and_2_out), .Q(d_ff_33_q), .reset(resetIN));  // open: Qn, preset
  LED led_30 (.in(d_ff_31_q));
  D_Flip_Flop d_ff_34 (.D(d_ff_31_q), .clk(and_2_out), .Q(d_ff_34_q), .reset(resetIN));  // open: Qn, preset
  LED led_31 (.in(d_ff_28_q));
  LED led_32 (.in(d_ff_32_q));
  and and_38 (and_38_out, not_3_out, 1'b0);
  or or_18 (or_18_out, and_37_out, and_38_out);
  D_Flip_Flop d_ff_35 (.D(or_18_out), .clk(and_1_out), .Q(d_ff_35_q), .reset(resetIN));  // open: Qn, preset
  and and_39 (and_39_out, ONoff, d_ff_30_q);
  and and_40 (and_40_out, not_4_out, 1'b0);
  or or_19 (or_19_out, and_39_out, and_40_out);
  D_Flip_Flop d_ff_36 (.D(or_19_out), .clk(and_1_out), .Q(d_ff_36_q), .reset(resetIN));  // open: Qn, preset
  LED led_33 (.in(d_ff_33_q));
  and and_41 (and_41_out, ONoff, d_ff_31_q);
  and and_42 (and_42_out, not_5_out, 1'b0);
  or or_20 (or_20_out, and_41_out, and_42_out);
  D_Flip_Flop d_ff_37 (.D(or_20_out), .clk(and_1_out), .Q(d_ff_37_q), .reset(resetIN));  // open: Qn, preset
  LED led_34 (.in(d_ff_34_q));
  LED led_35 (.in(d_ff_35_q));
  D_Flip_Flop d_ff_38 (.D(d_ff_35_q), .clk(and_2_out), .Q(d_ff_38_q), .reset(resetIN));  // open: Qn, preset
  LED led_36 (.in(d_ff_38_q));
  D_Flip_Flop d_ff_39 (.D(d_ff_7_q), .clk(and_2_out), .Q(splitOUT0[1]), .reset(resetIN));  // open: Qn, preset
  LED led_37 (.in(d_ff_36_q));
  D_Flip_Flop d_ff_40 (.D(d_ff_36_q), .clk(and_2_out), .Q(d_ff_40_q), .reset(resetIN));  // open: Qn, preset
  D_Flip_Flop d_ff_41 (.D(d_ff_19_q), .clk(and_2_out), .Q(splitOUT1[2]), .reset(resetIN));  // open: Qn, preset
  D_Flip_Flop d_ff_42 (.D(d_ff_8_q), .clk(and_2_out), .Q(splitOUT0[2]), .reset(resetIN));  // open: Qn, preset
  LED led_38 (.in(d_ff_37_q));
  D_Flip_Flop d_ff_43 (.D(d_ff_37_q), .clk(and_2_out), .Q(d_ff_43_q), .reset(resetIN));  // open: Qn, preset
  D_Flip_Flop d_ff_44 (.D(d_ff_9_q), .clk(and_2_out), .Q(splitOUT0[3]), .reset(resetIN));  // open: Qn, preset
  D_Flip_Flop d_ff_45 (.D(d_ff_2_q), .clk(and_2_out), .Q(splitOUT0[0]), .reset(resetIN));  // open: Qn, preset
  D_Flip_Flop d_ff_46 (.D(d_ff_15_q), .clk(and_2_out), .Q(splitOUT1[1]), .reset(resetIN));  // open: Qn, preset
  LED led_39 (.in(d_ff_40_q));
  D_Flip_Flop d_ff_47 (.D(d_ff_26_q), .clk(and_2_out), .Q(splitOUT2[2]), .reset(resetIN));  // open: Qn, preset
  LED led_40 (.in(d_ff_43_q));
  D_Flip_Flop d_ff_48 (.D(d_ff_16_q), .clk(and_2_out), .Q(splitOUT1[3]), .reset(resetIN));  // open: Qn, preset
  D_Flip_Flop d_ff_49 (.D(d_ff_29_q), .clk(and_2_out), .Q(splitOUT3[1]), .reset(resetIN));  // open: Qn, preset
  D_Flip_Flop d_ff_50 (.D(d_ff_22_q), .clk(and_2_out), .Q(splitOUT2[1]), .reset(resetIN));  // open: Qn, preset
  D_Flip_Flop d_ff_51 (.D(d_ff_33_q), .clk(and_2_out), .Q(splitOUT3[2]), .reset(resetIN));  // open: Qn, preset
  D_Flip_Flop d_ff_52 (.D(d_ff_27_q), .clk(and_2_out), .Q(splitOUT2[3]), .reset(resetIN));  // open: Qn, preset
  D_Flip_Flop d_ff_53 (.D(d_ff_10_q), .clk(and_2_out), .Q(splitOUT1[0]), .reset(resetIN));  // open: Qn, preset
  D_Flip_Flop d_ff_54 (.D(d_ff_38_q), .clk(and_2_out), .Q(splitOUT4[1]), .reset(resetIN));  // open: Qn, preset
  D_Flip_Flop d_ff_55 (.D(d_ff_40_q), .clk(and_2_out), .Q(splitOUT4[2]), .reset(resetIN));  // open: Qn, preset
  D_Flip_Flop d_ff_56 (.D(d_ff_34_q), .clk(and_2_out), .Q(splitOUT3[3]), .reset(resetIN));  // open: Qn, preset
  D_Flip_Flop d_ff_57 (.D(d_ff_17_q), .clk(and_2_out), .Q(splitOUT2[0]), .reset(resetIN));  // open: Qn, preset
  D_Flip_Flop d_ff_58 (.D(d_ff_43_q), .clk(and_2_out), .Q(splitOUT4[3]), .reset(resetIN));  // open: Qn, preset
  D_Flip_Flop d_ff_59 (.D(d_ff_24_q), .clk(and_2_out), .Q(splitOUT3[0]), .reset(resetIN));  // open: Qn, preset
  D_Flip_Flop d_ff_60 (.D(d_ff_32_q), .clk(and_2_out), .Q(splitOUT4[0]), .reset(resetIN));  // open: Qn, preset
endmodule

module myEncoder (
  input  onOFF,
  input  splitIN,
  input  resetIN,
  input  [3:0] splitIN0,
  input  [3:0] splitIN1,
  input  [3:0] splitIN2,
  input  [3:0] splitIN3,
  input  [3:0] splitIN4,
  output [3:0] mainOUT
);

  wire and_1_out, and_2_out, and_3_out, and_4_out, and_5_out, and_6_out, and_7_out, and_8_out, and_9_out,
       and_10_out, and_11_out, and_12_out, and_13_out, and_14_out, and_15_out, and_16_out, and_17_out,
       and_18_out, and_19_out, and_20_out, and_21_out, and_22_out, and_23_out, and_24_out, and_25_out,
       and_26_out, and_27_out, j_k_ff_1_q, j_k_ff_2_q, j_k_ff_3_q, not_1_out, not_2_out, not_3_out,
       not_4_out, not_5_out, not_6_out, not_7_out, not_8_out, not_9_out, not_10_out, or_1_out;

  and and_1 (and_1_out, j_k_ff_3_q, j_k_ff_1_q);
  or or_1 (or_1_out, resetIN, onOFF, and_1_out);
  and and_2 (and_2_out, j_k_ff_3_q, j_k_ff_2_q);
  J_K_Flip_Flop j_k_ff_1 (
    .J(and_2_out), .K(and_2_out), .clk(splitIN), .Q(j_k_ff_1_q), .reset(or_1_out));  // open: Qn, preset
  LED led_1 (.in(j_k_ff_1_q));
  J_K_Flip_Flop j_k_ff_2 (
    .J(j_k_ff_3_q), .K(j_k_ff_3_q), .clk(splitIN), .Q(j_k_ff_2_q), .reset(or_1_out));  // open: Qn, preset
  LED led_2 (.in(j_k_ff_2_q));
  J_K_Flip_Flop j_k_ff_3 (.J(1'b1), .K(1'b1), .clk(splitIN), .Q(j_k_ff_3_q), .reset(or_1_out));  // open: Qn, preset
  LED led_3 (.in(j_k_ff_3_q));
  not not_1 (not_1_out, j_k_ff_3_q);
  not not_2 (not_2_out, j_k_ff_2_q);
  not not_3 (not_3_out, j_k_ff_1_q);
  not not_4 (not_4_out, j_k_ff_2_q);
  not not_5 (not_5_out, j_k_ff_1_q);
  not not_6 (not_6_out, j_k_ff_3_q);
  not not_7 (not_7_out, j_k_ff_1_q);
  not not_8 (not_8_out, j_k_ff_1_q);
  not not_9 (not_9_out, j_k_ff_3_q);
  not not_10 (not_10_out, j_k_ff_2_q);
  and and_3 (and_3_out, not_1_out, not_2_out, not_3_out);
  and and_4 (and_4_out, j_k_ff_3_q, not_4_out, not_5_out);
  and and_5 (and_5_out, not_6_out, j_k_ff_2_q, not_7_out);
  and and_6 (and_6_out, j_k_ff_3_q, j_k_ff_2_q, not_8_out);
  and and_7 (and_7_out, not_9_out, not_10_out, j_k_ff_1_q);
  and and_8 (and_8_out, and_3_out, splitIN0[0]);
  and and_9 (and_9_out, and_3_out, splitIN0[1]);
  and and_10 (and_10_out, and_3_out, splitIN0[2]);
  and and_11 (and_11_out, and_3_out, splitIN0[3]);
  and and_12 (and_12_out, and_4_out, splitIN1[0]);
  and and_13 (and_13_out, and_4_out, splitIN1[1]);
  and and_14 (and_14_out, and_4_out, splitIN1[2]);
  and and_15 (and_15_out, and_4_out, splitIN1[3]);
  and and_16 (and_16_out, and_5_out, splitIN2[0]);
  and and_17 (and_17_out, and_5_out, splitIN2[1]);
  and and_18 (and_18_out, and_5_out, splitIN2[2]);
  and and_19 (and_19_out, and_5_out, splitIN2[3]);
  and and_20 (and_20_out, and_6_out, splitIN3[0]);
  and and_21 (and_21_out, and_6_out, splitIN3[1]);
  and and_22 (and_22_out, and_6_out, splitIN3[2]);
  and and_23 (and_23_out, and_6_out, splitIN3[3]);
  and and_24 (and_24_out, and_7_out, splitIN4[0]);
  and and_25 (and_25_out, and_7_out, splitIN4[1]);
  and and_26 (and_26_out, and_7_out, splitIN4[2]);
  and and_27 (and_27_out, and_7_out, splitIN4[3]);
  or or_2 (mainOUT[0], and_8_out, and_12_out, and_16_out, and_20_out, and_24_out);
  or or_3 (mainOUT[1], and_9_out, and_13_out, and_17_out, and_21_out, and_25_out);
  or or_4 (mainOUT[2], and_10_out, and_14_out, and_18_out, and_22_out, and_26_out);
  or or_5 (mainOUT[3], and_11_out, and_15_out, and_19_out, and_23_out, and_27_out);
endmodule

module mySelector (
  input  ONoff,
  input  [3:0] splitIN,
  input  [3:0] elapsedIN,
  output [3:0] O
);

  wire and_1_out, and_2_out, and_3_out, and_4_out, and_5_out, and_6_out, and_7_out, and_8_out, not_1_out;

  not not_1 (not_1_out, ONoff);
  and and_1 (and_1_out, not_1_out, splitIN[0]);
  and and_2 (and_2_out, not_1_out, splitIN[1]);
  and and_3 (and_3_out, not_1_out, splitIN[2]);
  and and_4 (and_4_out, not_1_out, splitIN[3]);
  and and_5 (and_5_out, ONoff, elapsedIN[0]);
  and and_6 (and_6_out, ONoff, elapsedIN[1]);
  and and_7 (and_7_out, ONoff, elapsedIN[2]);
  and and_8 (and_8_out, ONoff, elapsedIN[3]);
  or or_1 (O[0], and_1_out, and_5_out);
  or or_2 (O[1], and_2_out, and_6_out);
  or or_3 (O[2], and_3_out, and_7_out);
  or or_4 (O[3], and_4_out, and_8_out);
endmodule
